// Logisim project Exercicio2-Controle.circ as structural Verilog: 2 circuits, main circuit main
module main (
  input  in_1
);

  wire clock_1_out, unidade_de_controle_1_a, unidade_de_controle_1_alu_asrc, unidade_de_controle_1_alu_bsrc,
       unidade_de_controle_1_aluout, unidade_de_controle_1_asrc, unidade_de_controle_1_b,
       unidade_de_controle_1_bsrc, unidade_de_controle_1_ir, unidade_de_controle_1_madd,
       unidade_de_controle_1_mem, unidade_de_controle_1_memsrc, unidade_de_controle_1_pc,
       unidade_de_controle_1_regwrite;
  wire [15:0] counter_1_q, Madd_q, multiplexer_1_out;
  wire [31:0] A_q, adder_1_out, ALUout_q, B_q, bit_extender_1_out, bit_extender_2_out, bit_extender_3_out,
       IR_q, multiplexer_2_out, multiplexer_3_out, multiplexer_4_out, multiplexer_5_out,
       n32_registers_1_read_data_1, n32_registers_1_read_data_2, ram_1_data;
  wire [31:16] Madd_q_2;

  Clock clock_1 (.out(clock_1_out));
  Counter #(.width(16), .max('hffff)) counter_1 (
    .count(unidade_de_controle_1_pc), .Q(counter_1_q), .clk(clock_1_out), .clr(in_1));  // open: load, D, carry
  Multiplexer #(.width(16)) multiplexer_1 (
    .in0(counter_1_q), .in1(Madd_q), .out(multiplexer_1_out), .sel(unidade_de_controle_1_memsrc));  // open: en
  RAM #(.addrWidth(16), .dataWidth(32), .bus("separate")) ram_1 (
    .addr(multiplexer_1_out), .din(ALUout_q), .data(ram_1_data), .str(unidade_de_controle_1_mem),
    .clk(clock_1_out));  // open: sel, ld, clr
  Register #(.width(32)) IR (.D(ram_1_data), .en(unidade_de_controle_1_ir), .Q(IR_q), .clk(clock_1_out));  // open: clr
  assign bit_extender_1_out = {{7{1'b0}}, IR_q[24:0]};  // Bit_Extender bit_extender_1
  Unidade_de_Controle unidade_de_controle_1 (
    .OpCode(IR_q[31:30]), .Clock(clock_1_out), .Clear(in_1), .MEMsrc(unidade_de_controle_1_memsrc),
    .PC(unidade_de_controle_1_pc), .IR(unidade_de_controle_1_ir), .A(unidade_de_controle_1_a),
    .B(unidade_de_controle_1_b), .ALUout(unidade_de_controle_1_aluout), .Madd(unidade_de_controle_1_madd),
    .Mem(unidade_de_controle_1_mem), .Asrc(unidade_de_controle_1_asrc), .Bsrc(unidade_de_controle_1_bsrc),
    .ALU_Asrc(unidade_de_controle_1_alu_asrc), .ALU_Bsrc(unidade_de_controle_1_alu_bsrc),
    .RegWrite(unidade_de_controle_1_regwrite));
  _32_Registers u_32_registers_1 (
    .Read_Register_1(IR_q[24:20]), .Read_Register_2(IR_q[29:25]), .Write_Data(bit_extender_1_out),
    .RegWrite(unidade_de_controle_1_regwrite), .Write_Register(IR_q[29:25]),
    .Read_Data_1(n32_registers_1_read_data_1), .Read_Data_2(n32_registers_1_read_data_2), .Clock(clock_1_out));
  Multiplexer #(.width(32)) multiplexer_2 (
    .in0(n32_registers_1_read_data_1), .in1(ram_1_data), .out(multiplexer_2_out),
    .sel(unidade_de_controle_1_asrc));  // open: en
  Multiplexer #(.width(32)) multiplexer_3 (
    .in0(n32_registers_1_read_data_2), .in1(ram_1_data), .out(multiplexer_3_out),
    .sel(unidade_de_controle_1_bsrc));  // open: en
  assign bit_extender_2_out = {{22{1'b0}}, IR_q[19:10]};  // Bit_Extender bit_extender_2
  assign bit_extender_3_out = {{22{1'b0}}, IR_q[9:0]};  // Bit_Extender bit_extender_3
  Register #(.width(32)) A (
    .D(multiplexer_2_out), .en(unidade_de_controle_1_a), .Q(A_q), .clk(clock_1_out));  // open: clr
  Register #(.width(32)) B (
    .D(multiplexer_3_out), .en(unidade_de_controle_1_b), .Q(B_q), .clk(clock_1_out));  // open: clr
  Multiplexer #(.width(32)) multiplexer_4 (
    .in0(A_q), .in1(bit_extender_2_out), .out(multiplexer_4_out), .sel(unidade_de_controle_1_alu_asrc));  // open: en
  Multiplexer #(.width(32)) multiplexer_5 (
    .in0(B_q), .in1(bit_extender_3_out), .out(multiplexer_5_out), .sel(unidade_de_controle_1_alu_bsrc));  // open: en
  Adder #(.width(32)) adder_1 (.a(multiplexer_4_out), .b(multiplexer_5_out), .out(adder_1_out));  // open: cin, cout
  Register #(.width(32)) ALUout (
    .D(adder_1_out), .en(unidade_de_controle_1_aluout), .Q(ALUout_q), .clk(clock_1_out));  // open: clr
  Register #(.width(32)) Madd (
    .D(adder_1_out), .en(unidade_de_controle_1_madd), .Q({Madd_q_2, Madd_q}), .clk(clock_1_out));  // open: clr

  // Notes on the sheet:
  //   IR[24..0]
  //   IR[19..10]
  //   IR[9..0]
endmodule

module Unidade_de_Controle (
  input  [1:0] OpCode,
  input  Clock,
  input  Clear,
  output MEMsrc,
  output PC,
  output IR,
  output A,
  output B,
  output ALUout,
  output Madd,
  output Mem,
  output Asrc,
  output Bsrc,
  output ALU_Asrc,
  output ALU_Bsrc,
  output RegWrite
);

  wire and_1_out, and_2_out, and_3_out, and_4_out, and_5_out, and_6_out, and_9_out, and_10_out, and_11_out,
       and_12_out, and_13_out, and_14_out, and_15_out, and_16_out, and_17_out, and_18_out, decoder_1_out1,
       decoder_1_out2, decoder_1_out3, decoder_1_out4, decoder_1_out5, decoder_1_out6, not_1_out, or_1_out;
  wire [2:0] counter_1_q;

  Decoder #(.select(3)) decoder_1 (
    .out0(IR), .out1(decoder_1_out1), .out2(decoder_1_out2), .out3(decoder_1_out3), .out4(decoder_1_out4),
    .out5(decoder_1_out5), .out6(decoder_1_out6), .sel(counter_1_q));  // open: out7, en
  and and_1 (and_1_out, ~OpCode[0], ~OpCode[1], decoder_1_out1);  // AND_Gate
  or or_1 (or_1_out, and_1_out, and_3_out, and_2_out, and_4_out);
  and and_2 (and_2_out, ~OpCode[0], OpCode[1], decoder_1_out6);  // AND_Gate
  and and_3 (and_3_out, OpCode[0], ~OpCode[1], decoder_1_out1);  // AND_Gate
  and and_4 (and_4_out, OpCode[0], OpCode[1], decoder_1_out5);
  not not_1 (not_1_out, or_1_out);
  Counter #(.width(3), .max('h7)) counter_1 (
    .load(or_1_out), .D(3'b000), .count(not_1_out), .Q(counter_1_q), .clk(Clock), .clr(Clear));  // open: carry
  not not_2 (MEMsrc, IR);
  and and_5 (and_5_out, ~OpCode[0], OpCode[1]);  // AND_Gate
  and and_6 (and_6_out, decoder_1_out1, and_5_out);
  and and_7 (ALU_Bsrc, decoder_1_out2, and_5_out);
  or or_2 (A, and_6_out, Asrc, and_14_out);
  and and_8 (Asrc, decoder_1_out3, and_5_out);
  and and_9 (and_9_out, decoder_1_out4, and_5_out);
  or or_3 (B, and_6_out, and_9_out, and_14_out, and_17_out);
  or or_4 (ALUout, and_11_out, and_16_out);
  and and_10 (and_10_out, decoder_1_out6, and_5_out);
  and and_11 (and_11_out, decoder_1_out5, and_5_out);
  or or_5 (Madd, ALU_Bsrc, Asrc, and_13_out);
  and and_12 (and_12_out, OpCode[0], OpCode[1]);
  and and_13 (and_13_out, decoder_1_out2, and_12_out);
  and and_14 (and_14_out, decoder_1_out1, and_12_out);
  or or_6 (Mem, and_10_out, and_18_out);
  and and_15 (and_15_out, OpCode[0], ~OpCode[1]);  // AND_Gate
  and and_16 (and_16_out, decoder_1_out4, and_12_out);
  and and_17 (and_17_out, decoder_1_out3, and_12_out);
  and and_18 (and_18_out, decoder_1_out5, and_12_out);
  or or_7 (Bsrc, and_17_out, and_9_out);
  or or_8 (ALU_Asrc, and_13_out, Asrc);
  and and_19 (RegWrite, decoder_1_out1, and_15_out);

  assign PC = IR;

  // Notes on the sheet:
  //   Reg
  //   AddM
  //   AddR
  //   AddM
  //   AddR
  //   Reg
endmodule
