// Logisim project OAC2.circ as structural Verilog: 1 circuit, main circuit main
// A
module main (
);

  wire comparator_1_gt;
  wire [15:0] counter_1_q, multiplexer_1_out;
  wire [31:0] A_q, adder_1_out, AluOut_q, B_q, bit_extender_1_out, bit_extender_2_out, IR_q,
       multiplexer_2_out, multiplexer_3_out, n32_registers_1_read_data_1, n32_registers_1_read_data_2,
       ram_1_data, undriven;

  Counter #(.width(16), .max('hffff)) counter_1 (
    .Q(counter_1_q), .clk(adder_1_out[0]), .clr(adder_1_out[0]));  // open: load, D, count, carry
  Multiplexer #(.width(16)) multiplexer_1 (
    .in0(counter_1_q), .in1(AluOut_q[15:0]), .out(multiplexer_1_out));  // open: sel, en
  RAM #(.addrWidth(16), .dataWidth(32), .bus("separate")) ram_1 (.data(ram_1_data));  // open: addr, din, str, sel, clk, ld, clr
  assign bit_extender_1_out = {{16{1'b0}}, counter_1_q};  // Bit_Extender bit_extender_1
  Register #(.width(32)) IR (.D(ram_1_data), .Q(IR_q));  // open: en, clk, clr
  assign bit_extender_2_out = {{16{1'b0}}, IR_q[15:0]};  // Bit_Extender bit_extender_2
  _32_Registers u_32_registers_1 (
    .Read_Register_1(IR_q[20:16]), .Read_Register_2(IR_q[25:21]), .Read_Data_1(n32_registers_1_read_data_1),
    .Read_Data_2(n32_registers_1_read_data_2));  // open: Write_Data, RegWrite, Write_Register, Clock
  Register #(.width(32)) A (.D(n32_registers_1_read_data_1), .Q(A_q));  // open: en, clk, clr
  Register #(.width(32)) B (.D(n32_registers_1_read_data_2), .Q(B_q));  // open: en, clk, clr
  Comparator #(.width(32)) comparator_1 (.a(A_q), .b(B_q), .gt(comparator_1_gt), .lt(comparator_1_gt));  // open: eq
  Bit_Extender #(.in_width(4), .out_width(32)) bit_extender_3 (.in(4'b0100));  // open: out
  Multiplexer #(.width(32)) multiplexer_2 (.in1(undriven), .out(multiplexer_2_out));  // open: in0, sel, en
  Multiplexer #(.width(32)) multiplexer_3 (.in0(bit_extender_1_out), .out(multiplexer_3_out));  // open: in1, sel, en
  Adder #(.width(32)) adder_1 (.a(multiplexer_3_out), .b(multiplexer_2_out), .out(adder_1_out));  // open: cin, cout
  Register #(.width(32)) AluOut (.D(adder_1_out), .Q(AluOut_q));  // open: en, clk, clr
  // Pins of 1 and 32 bits meet at adder_1_out
  // Pins of 16 and 32 bits meet at AluOut_q
endmodule
